# Fritzing sketch arduino ethernet stepper motor2.3 (saved by Fritzing 0.9.3b)
breadboards: 1

parts:
  Pololu_Stepper_Motor_Driver = Pololu A4988 [package=SO16]
  Ethernet = MAGJACK-2 [package=magjack-19938]
  Power_12V = Power plug
  U3 = ENC28J60 [package=ssop28db]
  ATmega328 = ATmega328 [package=tqfp]
  R1 = Resistor [tolerance=±1% resistance=49.9 package="0805 [SMD]"]
  R2 = Resistor [tolerance=±1% resistance=49.9 package="0805 [SMD]"]
  R3 = Resistor [tolerance=±5% resistance=180 package="0805 [SMD]"]
  R4 = Resistor [tolerance=±5% resistance=180 package="0805 [SMD]"]
  C1 = Capacitor [part_number=10nF package=0805]
  L1 = Inductors [part_number="???? BREAD" package=0805]
  C2 = Capacitor [part_number=100nF package=0805]
  R5 = Resistor [tolerance=±1% resistance=49.9 package="0805 [SMD]"]
  R6 = Resistor [tolerance=±1% resistance=49.9 package="0805 [SMD]"]
  R7 = Resistor [tolerance=±1% resistance=2k package="0805 [SMD]"]
  C8 = Capacitor Polarized [part_number=10uF package=eia3216]
  C9 = Ceramic Capacitor [capacitance="100 nF" package="1206 [SMD, multilayer]"]
  R8 = Resistor [tolerance=±5% resistance=100k package="0805 [SMD]"]
  R9 = Resistor [tolerance=±5% resistance=10k package="0805 [SMD]"]
  S1 = Pushbutton [package="[THT]"]
  R10 = Resistor [tolerance=±5% resistance=10k package="0805 [SMD]"]
  XTAL1 = Crystal [frequency="25 MHz" package=THT]
  C10 = Ceramic Capacitor [capacitance=10pF package="1206 [SMD, multilayer]"]
  C11 = Ceramic Capacitor [capacitance=10pF package="1206 [SMD, multilayer]"]
  C4 = Ceramic Capacitor [capacitance="100 nF" package="0805 [SMD, multilayer]"]
  C5 = Ceramic Capacitor [capacitance="100 nF" package="0805 [SMD, multilayer]"]
  C6 = Ceramic Capacitor [capacitance="100 nF" package="0805 [SMD, multilayer]"]
  C7 = Ceramic Capacitor [capacitance="100 nF" package="0805 [SMD, multilayer]"]
  C12 = Ceramic Capacitor [capacitance=0.1µF package="0805 [SMD, multilayer]"]
  C13 = Ceramic Capacitor [capacitance=0.1µF package="0805 [SMD, multilayer]"]
  C14 = Ceramic Capacitor [capacitance=10pF package="1206 [SMD, multilayer]"]
  C15 = Ceramic Capacitor [capacitance=10pF package="1206 [SMD, multilayer]"]
  XTAL2 = Crystal [frequency="25 MHz" package=THT]
  C16 = Ceramic Capacitor [capacitance=0.1µF package="0805 [SMD, multilayer]"]
  LD1117 = V_REG_MIC2920 [part_number=LD1117SC-R package=sot223]
  R11 = Resistor [tolerance=±5% resistance=200 package="0805 [SMD]"]
  R12 = Resistor [tolerance=±5% resistance=120 package="0805 [SMD]"]
  C21 = Electrolytic Capacitor [capacitance=47µF voltage=16V package="0605 [SMD, electrolytic]"]
  C18 = Electrolytic Capacitor [capacitance=10µF voltage=16V package="0405 [SMD, electrolytic]"]
  C19 = Electrolytic Capacitor [capacitance=10µF voltage=6.3V package="0405 [SMD, electrolytic]"]
  C20 = Electrolytic Capacitor [capacitance=10µF voltage=6.3V package="0405 [SMD, electrolytic]"]
  M1 = Stepper Motor - Bipolar
  programmer_Serial_TTL = female pin header, 5 pins [form="♀ (female)"]
  J1 = AVR ISP 6 Pin [package=2x3-ns]
  J2 = female pin header, 2 pins [form="♀ (female)"]

nets:
  N1: Pololu_Stepper_Motor_Driver.RESET, Pololu_Stepper_Motor_Driver.SLEEP
  N2: Pololu_Stepper_Motor_Driver.STEP, ATmega328.PD3(INT1)
  N3: Pololu_Stepper_Motor_Driver.DIR, ATmega328.PD4(XCK_T0)
  GND: Pololu_Stepper_Motor_Driver.GND, Ethernet.SHIELD, Power_12V.GND, U3.VSS, U3.VSSRX, U3.VSSTX, U3.VSSPLL, U3.VSSOSC, ATmega328.GND, ATmega328.AGND, R3.Pin_0, R4.Pin_0, C1.2, C2.2, R7.Pin_0, C8.-, C9.0, S1.Pin_3, S1.Pin_4, C10.1, C11.1, C4.0, C5.0, C6.0, C7.0, C13.0, C14.1, C15.1, C16.0, R11.Pin_0, C21.-, C18.-, C19.-, C20.-, programmer_Serial_TTL.pin2, J1.6
  3.3V: Pololu_Stepper_Motor_Driver.VDD, U3.VDDTX, U3.VDDRX, U3.VDDPLL, U3.VDDOSC, U3.VDD, ATmega328.VCC, ATmega328.AVCC, L1.1, C9.1, R8.Pin_1, R9.Pin_1, R10.Pin_1, C4.1, C5.1, C6.1, C7.1, C16.1, LD1117.OUT, R12.Pin_1, C20.+, programmer_Serial_TTL.pin3, J2.pin1
  N4: Pololu_Stepper_Motor_Driver.1B, M1.D
  N5: Pololu_Stepper_Motor_Driver.1A, M1.B
  N6: Pololu_Stepper_Motor_Driver.2A, M1.C
  N7: Pololu_Stepper_Motor_Driver.2B, M1.A
  12V: Pololu_Stepper_Motor_Driver.VMOT, Power_12V.VCC, LD1117.IN, C21.+, C18.+
  N8: Ethernet.RD+, U3.TPIN+, R2.Pin_1
  N9: Ethernet.RD-, U3.TPIN-, R1.Pin_1
  N10: Ethernet.TD+, U3.TPOUT+, R5.Pin_0
  N11: Ethernet.TCT, L1.2, C2.1, R5.Pin_1, R6.Pin_1
  N12: Ethernet.TD-, U3.TPOUT-, R6.Pin_0
  N13: Ethernet.GLED-, R4.Pin_1
  N14: Ethernet.GLED+, U3.LEDA
  N15: Ethernet.YLED-, R3.Pin_1
  N16: Ethernet.YLED+, U3.LEDB
  N17: U3.VCAP, C8.+
  N18: U3.SO, ATmega328.PB4(MISO), J1.1
  N19: U3.SI, ATmega328.PB3(MOSI_OC2), J1.4
  N20: U3.SCK, ATmega328.PB5(SCK), J1.3
  N21: U3.CS, R8.Pin_0
  N22: U3.RESET, R9.Pin_0
  N23: U3.RBIAS, R7.Pin_1
  N24: U3.OSC1, XTAL1.pin_0, C10.0
  N25: U3.OSC2, XTAL1.pin_1, C11.0
  N26: ATmega328.PB6(XTAL1_TOSC1), C14.0, XTAL2.pin_1
  N27: ATmega328.PB7(XTAL2_TOSC2), C15.0, XTAL2.pin_0
  N28: ATmega328.AREF, C13.1
  N29: ATmega328.PC6(_RESET), S1.Pin_1, S1.Pin_2, R10.Pin_0, C12.0, J1.5
  N30: ATmega328.PD0(RXD), programmer_Serial_TTL.pin5
  N31: ATmega328.PD1(TXD), programmer_Serial_TTL.pin4
  N32: R1.Pin_0, R2.Pin_0, C1.1
  N33: C12.1, programmer_Serial_TTL.pin1
  N34: LD1117.GND, R11.Pin_1, R12.Pin_0, C19.+
  N35: J1.2, J2.pin2
